# Fritzing sketch HomeMatic_PIR (saved by Fritzing 0.9.3b)

parts:
  Bauteil1 = HC-SR501 Body Sensor Module
  WeMos_D1_Mini1 = WeMos D1 Mini
  S2 = Momentary Switch [package=ksa_sealed_tac_switch]
  HLK-PM2 = HLK-PM01

nets:
  VCC: Bauteil1.VCC, WeMos_D1_Mini1.5V, HLK-PM2.+Vo
  N1: Bauteil1.OUT, WeMos_D1_Mini1.D5
  N2: Bauteil1.GND, WeMos_D1_Mini1.G, S2.3, HLK-PM2.-Vo
  N3: WeMos_D1_Mini1.D7, S2.1

custom parts:
  HC-SR501 Body Sensor Module: Pyroelectric Infrared PIR Motion Sensor Detector Module
